# Fritzing sketch onboard control (saved by Fritzing 0.9.4)

parts:
  Part1 = Arduino Nano (Rev3.0)
  Part2 = 16-Channel 12-bit PWM Servo Driver - I2C [part_number=815]
  J1 = Basic Servo
  M1 = DC Motor
  Part3 = NRF24L01+ Breakout Board
  M2 = ESC

nets:
  GND: Part1.GND, Part2.GND, J1.gnd, Part3.GND, M2.GND
  N1: Part1.D9, Part3.CE
  N2: Part1.D10, Part3.CS
  N3: Part1.D11/MOSI, Part3.MOSI
  N4: Part1.D12/MISO, Part3.MISO
  5V: Part1.5V, Part2.VCC
  N5: Part1.A5, Part2.SCL
  N6: Part1.A4, Part2.SDA
  3V3: Part1.3V3, Part3.VCC
  N7: Part1.D13/SCK, Part3.SCK
  N8: Part2.PWM1, M2.DATA
  N9: Part2.5.0V, J1.vcc, M2.pin_8
  N10: Part2.PWM0, J1.pulse
  N11: M1.pin_1, M2.U
  N12: M1.pin_2, M2.W

notes:
  USB to onboard computer

custom parts:
  16-Channel 12-bit PWM Servo Driver - I2C: You want to make a cool robot, maybe a hexapod walker, or maybe just a piece of art with a lot of moving parts. Or maybe you want to drive a lot of LEDs with precise PWM output. Using only two pins, control 16 free-running PWM outputs! You can even chain up 62 breakouts to control up to 992 PWM outputs.
