# Fritzing sketch remote (saved by Fritzing 0.9.4)

parts:
  Part1 = Arduino Nano (Rev3.0)
  Part2 = NRF24L01+ Breakout Board
  Grove1 = Grove OLED 128x96
  Part3 = Black Joystick KY-023
  Part4 = Black Joystick KY-023

nets:
  GND: Part1.GND, Part2.GND
  N1: Part1.D2, Part4.SW
  N2: Part1.D3, Part3.SW
  N3: Part1.D9, Part2.CE
  N4: Part1.D10, Part2.CS
  N5: Part1.D11/MOSI, Part2.MOSI
  N6: Part1.D12/MISO, Part2.MISO
  N7: Part1.A5, Grove1.SCL
  N8: Part1.A4, Grove1.SDA
  N9: Part1.A3, Part3.VRy
  N10: Part1.A2, Part3.VRx
  N11: Part1.A1, Part4.VRy
  N12: Part1.A0, Part4.VRx
  3V3: Part1.3V3, Part2.VCC
  N13: Part1.D13/SCK, Part2.SCK

custom parts:
  Black Joystick KY-023: Description: The joystick is a combination of 2 analoog potentiometer and a digital switch. Arduino GND --> Module pin - Arduino +5V --> Module pin +5V Arduino Analoog 0 --> Module VRx Arduino Analoog 1 --> Module VRy Arduino Digital --> Module SW Dimensions: 1" x 1.25"
